// Logisim project CPU.circ as structural Verilog: 16 circuits, main circuit full_adder
module encoder (
  input  [15:0] in_1,
  output [3:0] out_2
);

  or or_1 (out_2[0], in_1[1], in_1[3], in_1[5], in_1[7], in_1[9], in_1[11], in_1[13], in_1[15]);
  or or_2 (out_2[1], in_1[2], in_1[3], in_1[6], in_1[7], in_1[10], in_1[11], in_1[14], in_1[15]);
  or or_3 (out_2[2], in_1[4], in_1[5], in_1[6], in_1[7], in_1[12], in_1[13], in_1[14], in_1[15]);
  or or_4 (out_2[3], in_1[8], in_1[9], in_1[10], in_1[11], in_1[12], in_1[13], in_1[14], in_1[15]);
endmodule

module de_coder (
  input  [3:0] in_1,
  output [15:0] out_2
);

  wire [3:0] not_1_out;

  assign not_1_out = ~in_1;  // NOT_Gate not_1, 4 bits wide
  and and_1 (out_2[0], not_1_out[0], not_1_out[1], not_1_out[2], not_1_out[3]);
  and and_2 (out_2[1], in_1[0], not_1_out[1], not_1_out[2], not_1_out[3]);
  and and_3 (out_2[2], not_1_out[0], in_1[1], not_1_out[2], not_1_out[3]);
  and and_4 (out_2[3], in_1[0], in_1[1], not_1_out[2], not_1_out[3]);
  and and_5 (out_2[4], not_1_out[0], not_1_out[1], in_1[2], not_1_out[3]);
  and and_6 (out_2[5], in_1[0], not_1_out[1], in_1[2], not_1_out[3]);
  and and_7 (out_2[6], not_1_out[0], in_1[1], in_1[2], not_1_out[3]);
  and and_8 (out_2[7], in_1[0], in_1[1], in_1[2], not_1_out[3]);
  and and_9 (out_2[8], not_1_out[0], not_1_out[1], not_1_out[2], in_1[3]);
  and and_10 (out_2[9], in_1[0], not_1_out[1], not_1_out[2], in_1[3]);
  and and_11 (out_2[10], not_1_out[0], in_1[1], not_1_out[2], in_1[3]);
  and and_12 (out_2[11], in_1[0], in_1[1], not_1_out[2], in_1[3]);
  and and_13 (out_2[12], not_1_out[0], not_1_out[1], in_1[2], in_1[3]);
  and and_14 (out_2[13], in_1[0], not_1_out[1], in_1[2], in_1[3]);
  and and_15 (out_2[14], not_1_out[0], in_1[1], in_1[2], in_1[3]);
  and and_16 (out_2[15], in_1[0], in_1[1], in_1[2], in_1[3]);
endmodule

module controlled_invertor (
  input  [7:0] D,
  input  I,
  output [7:0] Q
);

  xor xor_1 (Q[0], D[0], I);
  xor xor_2 (Q[1], D[1], I);
  xor xor_3 (Q[2], D[2], I);
  xor xor_4 (Q[3], D[3], I);
  xor xor_5 (Q[4], D[4], I);
  xor xor_6 (Q[5], D[5], I);
  xor xor_7 (Q[6], D[6], I);
  xor xor_8 (Q[7], D[7], I);
endmodule

module parity_detector (
  input  [7:0] D,
  output P
);

  wire xor_1_out, xor_2_out, xor_3_out, xor_4_out, xor_5_out, xor_6_out;

  xor xor_1 (xor_1_out, D[0], D[1]);
  xor xor_2 (xor_2_out, D[2], D[3]);
  xor xor_3 (xor_3_out, D[4], D[5]);
  xor xor_4 (xor_4_out, D[6], D[7]);
  xor xor_5 (xor_5_out, xor_1_out, xor_2_out);
  xor xor_6 (xor_6_out, xor_3_out, xor_4_out);
  xor xor_7 (P, xor_5_out, xor_6_out);
endmodule

module half_adder (
  input  A,
  input  B,
  output Co,
  output S
);

  and and_1 (Co, A, B);
  xor xor_1 (S, A, B);
endmodule

module full_adder (
  input  Ci,
  input  A,
  input  B,
  output Co,
  output O
);

  wire xor_1_out;

  xor xor_1 (xor_1_out, A, B);
  xor xor_2 (O, Ci, xor_1_out);
endmodule

module ripple_adder_8_bit (
  input  Ci,
  input  [7:0] A,
  input  [7:0] B,
  output [7:0] O,
  output Co
);

  wire full_adder_1_co, full_adder_2_co, full_adder_3_co, full_adder_4_co, full_adder_5_co, full_adder_6_co,
       full_adder_7_co;

  full_adder full_adder_1 (.Ci(Ci), .A(A[0]), .B(B[0]), .Co(full_adder_1_co), .O(O[0]));
  full_adder full_adder_2 (.Ci(full_adder_1_co), .A(A[1]), .B(B[1]), .Co(full_adder_2_co), .O(O[1]));
  full_adder full_adder_3 (.Ci(full_adder_2_co), .A(A[2]), .B(B[2]), .Co(full_adder_3_co), .O(O[2]));
  full_adder full_adder_4 (.Ci(full_adder_3_co), .A(A[3]), .B(B[3]), .Co(full_adder_4_co), .O(O[3]));
  full_adder full_adder_5 (.Ci(full_adder_4_co), .A(A[4]), .B(B[4]), .Co(full_adder_5_co), .O(O[4]));
  full_adder full_adder_6 (.Ci(full_adder_5_co), .A(A[5]), .B(B[5]), .Co(full_adder_6_co), .O(O[5]));
  full_adder full_adder_7 (.Ci(full_adder_6_co), .A(A[6]), .B(B[6]), .Co(full_adder_7_co), .O(O[6]));
  full_adder full_adder_8 (.Ci(full_adder_7_co), .A(A[7]), .B(B[7]), .Co(Co), .O(O[7]));
endmodule

module arithmetic_unit_8_bit (
  input  [7:0] A,
  input  [7:0] B,
  input  EO,
  input  SU,
  output [7:0] Q,
  output Co,
  output [7:0] ST
);

  wire [7:0] xor_8_out;

  xor xor_1 (xor_8_out[7], SU, B[7]);
  xor xor_2 (xor_8_out[6], SU, B[6]);
  xor xor_3 (xor_8_out[5], SU, B[5]);
  xor xor_4 (xor_8_out[4], SU, B[4]);
  xor xor_5 (xor_8_out[3], SU, B[3]);
  ripple_adder_8_bit ripple_adder_8_bit_1 (.Ci(SU), .A(A), .B(xor_8_out), .O(ST), .Co(Co));
  xor xor_6 (xor_8_out[2], SU, B[2]);
  assign Q = EO ? ST : 8'bz;  // Controlled_Buffer controlled_buffer_1
  xor xor_7 (xor_8_out[1], SU, B[1]);
  xor xor_8 (xor_8_out[0], SU, B[0]);
endmodule

module s_latch (
  input  S,
  output Q
);

  or or_1 (Q, S, Q);
endmodule

module sr_latch (
  input  R,
  input  S,
  output Q,
  output NQ
);

  nor nor_1 (Q, R, NQ);
  nor nor_2 (NQ, Q, S);
endmodule

module d_latch (
  input  D,
  input  E,
  output Q,
  output NQ
);

  wire and_1_out, and_2_out, not_1_out;

  not not_1 (not_1_out, D);
  and and_1 (and_1_out, not_1_out, E);
  and and_2 (and_2_out, E, D);
  sr_latch sr_latch_1 (.R(and_1_out), .S(and_2_out), .Q(Q), .NQ(NQ));
endmodule

module d_flip_flop (
  input  D,
  input  RCLK,
  output Q,
  output NQ
);

  D_Flip_Flop d_ff_1 (.D(D), .clk(RCLK), .Q(Q), .Qn(NQ));  // open: preset, reset
endmodule

module data_register (
  input  D,
  input  L,
  input  CLK,
  output Q
);

  wire and_1_out, and_2_out, not_1_out, or_1_out;

  not not_1 (not_1_out, L);
  and and_1 (and_1_out, Q, not_1_out);
  and and_2 (and_2_out, D, L);
  or or_1 (or_1_out, and_1_out, and_2_out);
  d_flip_flop d_flip_flop_1 (.D(or_1_out), .RCLK(CLK), .Q(Q));  // open: NQ
endmodule

module data_register_8_bit (
  input  [7:0] D,
  input  L,
  input  E,
  input  CLK,
  output [7:0] Q,
  output [7:0] ST
);

  data_register data_register_1 (.D(D[0]), .L(L), .CLK(CLK), .Q(ST[0]));
  data_register data_register_2 (.D(D[1]), .L(L), .CLK(CLK), .Q(ST[1]));
  data_register data_register_3 (.D(D[2]), .L(L), .CLK(CLK), .Q(ST[2]));
  data_register data_register_4 (.D(D[3]), .L(L), .CLK(CLK), .Q(ST[3]));
  data_register data_register_5 (.D(D[4]), .L(L), .CLK(CLK), .Q(ST[4]));
  data_register data_register_6 (.D(D[5]), .L(L), .CLK(CLK), .Q(ST[5]));
  data_register data_register_7 (.D(D[6]), .L(L), .CLK(CLK), .Q(ST[6]));
  data_register data_register_8 (.D(D[7]), .L(L), .CLK(CLK), .Q(ST[7]));
  assign Q = E ? ST : 8'bz;  // Controlled_Buffer controlled_buffer_1
endmodule

module ram_8_bit_16_byte (
  input  E,
  input  L,
  input  CLK,
  input  [7:0] D,
  input  [3:0] A,
  output [7:0] Q
);

  wire and_1_out, and_2_out, and_3_out, and_4_out, and_5_out, and_6_out, and_7_out, and_8_out, and_9_out,
       and_10_out, and_11_out, and_12_out, and_13_out, and_14_out, and_15_out, and_16_out, and_17_out,
       and_18_out, and_19_out, and_20_out, and_21_out, and_22_out, and_23_out, and_24_out, and_25_out,
       and_26_out, and_27_out, and_28_out, and_29_out, and_30_out, and_31_out, and_32_out;
  wire [3:0] not_1_out;

  and and_1 (and_1_out, not_1_out[0], not_1_out[1], not_1_out[2], not_1_out[3], L);
  and and_2 (and_2_out, A[0], not_1_out[1], not_1_out[2], not_1_out[3], L);
  and and_3 (and_3_out, not_1_out[0], A[1], not_1_out[2], not_1_out[3], L);
  and and_4 (and_4_out, A[0], A[1], not_1_out[2], not_1_out[3], L);
  and and_5 (and_5_out, not_1_out[0], not_1_out[1], A[2], not_1_out[3], L);
  and and_6 (and_6_out, A[0], not_1_out[1], A[2], not_1_out[3], L);
  and and_7 (and_7_out, not_1_out[0], A[1], A[2], not_1_out[3], L);
  and and_8 (and_8_out, A[0], A[1], A[2], not_1_out[3], L);
  and and_9 (and_9_out, not_1_out[0], not_1_out[1], not_1_out[2], A[3], L);
  and and_10 (and_10_out, A[0], not_1_out[2], not_1_out[1], A[3], L);
  and and_11 (and_11_out, not_1_out[3], A[1], not_1_out[1], A[3], L);
  and and_12 (and_12_out, A[0], A[1], not_1_out[1], A[3], L);
  and and_13 (and_13_out, not_1_out[3], not_1_out[2], A[2], A[3], L);
  and and_14 (and_14_out, A[1], not_1_out[2], A[2], A[3], L);
  and and_15 (and_15_out, not_1_out[3], A[1], A[2], A[3], L);
  and and_16 (and_16_out, A[0], A[1], A[2], A[3], L);
  assign not_1_out = ~A;  // NOT_Gate not_1, 4 bits wide
  and and_17 (and_17_out, not_1_out[0], not_1_out[1], not_1_out[2], not_1_out[3], E);
  and and_18 (and_18_out, A[0], not_1_out[1], not_1_out[2], not_1_out[3], E);
  and and_19 (and_19_out, not_1_out[0], A[1], not_1_out[2], not_1_out[3], E);
  and and_20 (and_20_out, A[0], A[1], not_1_out[2], not_1_out[3], E);
  and and_21 (and_21_out, not_1_out[0], not_1_out[1], A[2], not_1_out[3], E);
  and and_22 (and_22_out, A[0], not_1_out[1], A[2], not_1_out[3], E);
  and and_23 (and_23_out, not_1_out[0], A[1], A[2], not_1_out[3], E);
  and and_24 (and_24_out, A[0], A[1], A[2], not_1_out[3], E);
  and and_25 (and_25_out, not_1_out[0], not_1_out[1], not_1_out[2], A[3], E);
  and and_26 (and_26_out, A[0], not_1_out[2], not_1_out[1], A[3], E);
  and and_27 (and_27_out, not_1_out[3], A[1], not_1_out[1], A[3], E);
  and and_28 (and_28_out, A[0], A[1], not_1_out[1], A[3], E);
  and and_29 (and_29_out, not_1_out[3], not_1_out[2], A[2], A[3], E);
  and and_30 (and_30_out, A[1], not_1_out[2], A[2], A[3], E);
  and and_31 (and_31_out, not_1_out[3], A[1], A[2], A[3], E);
  and and_32 (and_32_out, A[0], A[1], A[2], A[3], E);
  data_register_8_bit data_register_8_bit_1 (.D(D), .L(and_1_out), .E(and_17_out), .CLK(CLK), .Q(Q));  // open: ST
  data_register_8_bit data_register_8_bit_2 (.D(D), .L(and_2_out), .E(and_18_out), .CLK(CLK), .Q(Q));  // open: ST
  data_register_8_bit data_register_8_bit_3 (.D(D), .L(and_3_out), .E(and_19_out), .CLK(CLK), .Q(Q));  // open: ST
  data_register_8_bit data_register_8_bit_4 (.D(D), .L(and_4_out), .E(and_20_out), .CLK(CLK), .Q(Q));  // open: ST
  data_register_8_bit data_register_8_bit_5 (.D(D), .L(and_5_out), .E(and_21_out), .CLK(CLK), .Q(Q));  // open: ST
  data_register_8_bit data_register_8_bit_6 (.D(D), .L(and_6_out), .E(and_22_out), .CLK(CLK), .Q(Q));  // open: ST
  data_register_8_bit data_register_8_bit_7 (.D(D), .L(and_7_out), .E(and_23_out), .CLK(CLK), .Q(Q));  // open: ST
  data_register_8_bit data_register_8_bit_8 (.D(D), .L(and_8_out), .E(and_24_out), .CLK(CLK), .Q(Q));  // open: ST
  data_register_8_bit data_register_8_bit_9 (.D(D), .L(and_9_out), .E(and_25_out), .CLK(CLK), .Q(Q));  // open: ST
  data_register_8_bit data_register_8_bit_10 (.D(D), .L(and_10_out), .E(and_26_out), .CLK(CLK), .Q(Q));  // open: ST
  data_register_8_bit data_register_8_bit_11 (.D(D), .L(and_11_out), .E(and_27_out), .CLK(CLK), .Q(Q));  // open: ST
  data_register_8_bit data_register_8_bit_12 (.D(D), .L(and_12_out), .E(and_28_out), .CLK(CLK), .Q(Q));  // open: ST
  data_register_8_bit data_register_8_bit_13 (.D(D), .L(and_13_out), .E(and_29_out), .CLK(CLK), .Q(Q));  // open: ST
  data_register_8_bit data_register_8_bit_14 (.D(D), .L(and_14_out), .E(and_30_out), .CLK(CLK), .Q(Q));  // open: ST
  data_register_8_bit data_register_8_bit_15 (.D(D), .L(and_15_out), .E(and_31_out), .CLK(CLK), .Q(Q));  // open: ST
  data_register_8_bit data_register_8_bit_16 (.D(D), .L(and_16_out), .E(and_32_out), .CLK(CLK), .Q(Q));  // open: ST
endmodule

module main (
  input  PB,
  input  HLT,
  input  AL,
  input  AE,
  input  RE,
  input  RL,
  input  EO,
  input  SU,
  input  BL,
  input  BE,
  input  IL,
  input  IE
);

  wire and_1_out, CLK_out, not_1_out;
  wire [3:0] IR_st, IR_st_2;
  wire [7:0] A_st, ALU_st, B_st, dipswitch_1_sw8, IR_q, ram_8_bit_16_byte_1_q;

  Clock CLK (.out(CLK_out));
  not not_1 (not_1_out, HLT);
  and and_1 (and_1_out, CLK_out, not_1_out);
  LedBar #(.matrixcols(4)) ledbar_1 (.led0(IR_st_2[3]), .led1(IR_st_2[2]), .led2(IR_st_2[1]), .led3(IR_st_2[0]));
  DipSwitch dipswitch_1 (
    .sw1(dipswitch_1_sw8[7]), .sw2(dipswitch_1_sw8[6]), .sw3(dipswitch_1_sw8[5]), .sw4(dipswitch_1_sw8[4]),
    .sw5(dipswitch_1_sw8[3]), .sw6(dipswitch_1_sw8[2]), .sw7(dipswitch_1_sw8[1]), .sw8(dipswitch_1_sw8[0]));
  ram_8_bit_16_byte ram_8_bit_16_byte_1 (.E(RE), .L(RL), .CLK(and_1_out), .Q(ram_8_bit_16_byte_1_q));  // open: D, A
  LedBar #(.matrixcols(4)) ledbar_2 (.led0(IR_st[3]), .led1(IR_st[2]), .led2(IR_st[1]), .led3(IR_st[0]));
  data_register_8_bit IR (.D(ram_8_bit_16_byte_1_q), .L(IL), .E(IE), .CLK(and_1_out), .Q(IR_q), .ST({IR_st_2, IR_st}));
  assign ram_8_bit_16_byte_1_q = PB ? dipswitch_1_sw8 : 8'bz;  // Controlled_Buffer controlled_buffer_1
  assign ram_8_bit_16_byte_1_q = IE ? {4'b0000, IR_q[3:0]} : 8'bz;  // Controlled_Buffer controlled_buffer_2
  LedBar ledbar_3 (
    .led0(ram_8_bit_16_byte_1_q[7]), .led1(ram_8_bit_16_byte_1_q[6]), .led2(ram_8_bit_16_byte_1_q[5]),
    .led3(ram_8_bit_16_byte_1_q[4]), .led4(ram_8_bit_16_byte_1_q[3]), .led5(ram_8_bit_16_byte_1_q[2]),
    .led6(ram_8_bit_16_byte_1_q[1]), .led7(ram_8_bit_16_byte_1_q[0]));
  LedBar ledbar_4 (
    .led0(A_st[7]), .led1(A_st[6]), .led2(A_st[5]), .led3(A_st[4]), .led4(A_st[3]), .led5(A_st[2]),
    .led6(A_st[1]), .led7(A_st[0]));
  LedBar ledbar_5 (
    .led0(ALU_st[7]), .led1(ALU_st[6]), .led2(ALU_st[5]), .led3(ALU_st[4]), .led4(ALU_st[3]),
    .led5(ALU_st[2]), .led6(ALU_st[1]), .led7(ALU_st[0]));
  LedBar ledbar_6 (
    .led0(B_st[7]), .led1(B_st[6]), .led2(B_st[5]), .led3(B_st[4]), .led4(B_st[3]), .led5(B_st[2]),
    .led6(B_st[1]), .led7(B_st[0]));
  data_register_8_bit A (
    .D(ram_8_bit_16_byte_1_q), .L(AL), .E(AE), .CLK(and_1_out), .Q(ram_8_bit_16_byte_1_q), .ST(A_st));
  arithmetic_unit_8_bit ALU (.A(A_st), .B(B_st), .EO(EO), .SU(SU), .Q(ram_8_bit_16_byte_1_q), .ST(ALU_st));  // open: Co
  data_register_8_bit B (
    .D(ram_8_bit_16_byte_1_q), .L(BL), .E(BE), .CLK(and_1_out), .Q(ram_8_bit_16_byte_1_q), .ST(B_st));

  // Notes on the sheet:
  //   BUS
endmodule
